// Logisim project lesson2.circ as structural Verilog
module halfAdder (
  input  A,
  input  B,
  output sum,
  output carry
);

  and and_1 (carry, A, B);
  xor xor_1 (sum, A, B);
endmodule

module fullAdder (
  input  A,
  input  B,
  input  C,
  output sum,
  output carry
);

  wire halfadder_1_carry, halfadder_1_sum, halfadder_2_carry;

  halfAdder halfadder_1 (.A(A), .B(B), .sum(halfadder_1_sum), .carry(halfadder_1_carry));
  halfAdder halfadder_2 (.A(C), .B(halfadder_1_sum), .sum(sum), .carry(halfadder_2_carry));
  or or_1 (carry, halfadder_1_carry, halfadder_2_carry);
endmodule

module fourBitAdder (
  input  [3:0] A,
  input  Cin,
  input  [3:0] B,
  output [3:0] sum,
  output carry
);

  wire fulladder_1_carry, fulladder_2_carry, fulladder_3_carry;

  fullAdder fulladder_1 (.A(A[0]), .B(B[0]), .C(Cin), .sum(sum[0]), .carry(fulladder_1_carry));
  fullAdder fulladder_2 (.A(A[1]), .B(B[1]), .C(fulladder_1_carry), .sum(sum[1]), .carry(fulladder_2_carry));
  fullAdder fulladder_3 (.A(A[2]), .B(B[2]), .C(fulladder_2_carry), .sum(sum[2]), .carry(fulladder_3_carry));
  fullAdder fulladder_4 (.A(A[3]), .B(B[3]), .C(fulladder_3_carry), .sum(sum[3]), .carry(carry));
endmodule

module fourBitIncrementer (
  input  [3:0] A,
  output [3:0] Y
);

  fourBitAdder fourbitadder_1 (.A(A), .B(4'b0001), .sum(Y));  // open: Cin, carry
endmodule

module fourBitSubstractor (
  input  [3:0] A,
  input  [3:0] B,
  output [3:0] Y,
  output carry
);

  wire [3:0] not_1_out;

  assign not_1_out = ~B;  // NOT_Gate not_1, 4 bits wide
  fourBitAdder fourbitadder_1 (.A(A), .Cin(1'b1), .B(not_1_out), .sum(Y), .carry(carry));
endmodule

module fourBitAdderSubstractor (
  input  [3:0] A,
  input  [3:0] B,
  input  K,
  output [3:0] Y,
  output carry
);

  wire [3:0] multiplexer_1_out, not_1_out;

  assign not_1_out = ~B;  // NOT_Gate not_1, 4 bits wide
  Multiplexer #(.width(4), .enable("false")) multiplexer_1 (.in0(B), .in1(not_1_out), .out(multiplexer_1_out), .sel(K));
  fourBitAdder fourbitadder_1 (.A(A), .Cin(K), .B(multiplexer_1_out), .sum(Y), .carry(carry));
endmodule

module overflow (
  input  [3:0] A,
  input  [3:0] B,
  input  addOrSub,
  output V,
  output [3:0] Y
);

  wire bitselector_1_out, bitselector_2_out;

  BitSelector #(.width(4)) bitselector_1 (.in(A), .out(bitselector_1_out), .sel(2'b11));
  xor xor_1 (V, bitselector_1_out, bitselector_2_out);
  BitSelector #(.width(4)) bitselector_2 (.in(Y), .out(bitselector_2_out), .sel(2'b11));
  fourBitAdderSubstractor fourbitaddersubstractor_1 (.A(A), .B(B), .K(addOrSub), .Y(Y));  // open: carry
endmodule

module equalityComp (
  input  [3:0] A,
  input  [3:0] B,
  output Y
);

  wire xnor_1_out, xnor_2_out, xnor_3_out, xnor_4_out;

  xnor xnor_1 (xnor_1_out, A[0], B[0]);
  xnor xnor_2 (xnor_2_out, A[1], B[1]);
  xnor xnor_3 (xnor_3_out, A[2], B[2]);
  xnor xnor_4 (xnor_4_out, A[3], B[3]);
  and and_1 (Y, xnor_1_out, xnor_2_out, xnor_3_out, xnor_4_out);
endmodule
